// Logisim project brainfuck.circ as structural Verilog: 6 circuits, main circuit main
module main (
);

  wire and_1_out, and_2_out, and_3_out, and_4_out, and_5_out, and_6_out, and_7_out, and_8_out, and_9_out,
       clock_1_out, clock_2_out, clock_3_out, counter_1_q, decoder_2_out2, decoder_2_out3, decoder_2_out6,
       decoder_2_out7, Direction, DisplayValue, ExecuteCLK, HasChar, InstructionCLK, LoopBack,
       MemoryWriteEnable, MemPointerDown, MemPointerUp, multiplexer_1_out, multiplexer_2_out,
       multiplexer_3_out, multiplexer_4_out, nand_1_out, nand_2_out, not_1_out, not_3_out, not_4_out,
       or_1_out, or_2_out, or_3_out, or_4_out, ReadChar, SearchCLK, Searching, SkipLoop, zero_1_out_2,
       zero_2_out_2, zero_3_out_2;
  wire [2:0] Instruction;
  wire [6:0] counter_2_q, counter_3_q, decrease7_1_out_2, increase7_1_out_2, InputChar, multiplexer_5_out,
       Value;
  wire [15:0] decrease16_1_out_2, InstructionPointer_q, MemoryPointer_q;

  Clock clock_1 (.out(clock_1_out));
  TTY tty_1 (.data(Value), .clk(and_1_out));  // open: we, clr
  and and_1 (and_1_out, DisplayValue, ExecuteCLK);
  nand nand_1 (nand_1_out, ReadChar, ~HasChar);  // NAND_Gate
  Keyboard keyboard_1 (.clk(InstructionCLK), .re(ReadChar), .avail(HasChar), .data(InputChar));  // open: clr
  LED led_1 (.in(ReadChar));
  and and_2 (and_2_out, clock_1_out, nand_1_out, ~Searching);  // AND_Gate
  Decoder #(.enable("false")) decoder_1 (.out0(InstructionCLK), .out1(ExecuteCLK), .sel(counter_1_q));
  Counter #(.max('h1), .width(1)) counter_1 (.Q(counter_1_q), .clk(and_2_out));  // open: load, D, count, carry, up, clr
  nand nand_2 (nand_2_out, ~Direction, Searching);  // NAND_Gate
  Counter #(.max('hffff), .width(16)) InstructionPointer (
    .Q(InstructionPointer_q), .up(nand_2_out), .clk(or_1_out));  // open: load, D, count, carry, clr
  or or_1 (or_1_out, SearchCLK, and_3_out);
  and and_3 (and_3_out, InstructionCLK, ~Searching);  // AND_Gate
  ROM #(.addrWidth(16), .dataWidth(3)) Programm (.addr(InstructionPointer_q), .data(Instruction));
  Multiplexer #(.select(3)) multiplexer_1 (
    .in0(1'b0), .in1(1'b0), .in2(1'b0), .in3(1'b0), .in4(1'b0), .in5(1'b0), .in6(1'b1), .in7(1'b1),
    .out(multiplexer_1_out), .sel(Instruction));
  Multiplexer #(.select(3)) multiplexer_2 (
    .in0(1'b0), .in1(1'b0), .in2(1'b0), .in3(1'b0), .in4(1'b0), .in5(1'b0), .in6(1'b1), .in7(1'b1),
    .out(multiplexer_2_out), .sel(Instruction));
  and and_4 (and_4_out, Direction, multiplexer_1_out);
  and and_5 (and_5_out, not_3_out, multiplexer_2_out);
  INCREASE7 increase7_1 (.in_1(Value), .out_2(increase7_1_out_2));
  DECREASE7 decrease7_1 (.in_1(Value), .out_2(decrease7_1_out_2));
  or or_2 (or_2_out, and_4_out, SkipLoop);
  Clock clock_2 (.out(clock_2_out));
  or or_3 (or_3_out, and_5_out, LoopBack);
  Clock clock_3 (.out(clock_3_out));
  or or_4 (or_4_out, MemPointerDown, MemPointerUp);
  Multiplexer #(.select(3)) multiplexer_3 (
    .in6(1'b1), .in7(1'b0), .out(multiplexer_3_out), .sel(Instruction));  // open: in0, in1, in2, in3, in4, in5
  Counter #(.max('h7f), .width(7)) counter_2 (
    .count(or_2_out), .Q(counter_2_q), .up(multiplexer_3_out), .clk(clock_2_out));  // open: load, D, carry, clr
  ZERO zero_1 (.in_1(counter_2_q), .out_2(zero_1_out_2));
  Multiplexer #(.select(3)) multiplexer_4 (
    .in6(1'b0), .in7(1'b1), .out(multiplexer_4_out), .sel(Instruction));  // open: in0, in1, in2, in3, in4, in5
  Counter #(.max('h7f), .width(7)) counter_3 (
    .count(or_3_out), .Q(counter_3_q), .up(multiplexer_4_out), .clk(clock_3_out));  // open: load, D, carry, clr
  ZERO zero_2 (.in_1(counter_3_q), .out_2(zero_2_out_2));
  and and_6 (and_6_out, or_4_out, ExecuteCLK);
  Multiplexer #(.select(3), .width(7)) multiplexer_5 (
    .in2(increase7_1_out_2), .in3(decrease7_1_out_2), .in5(InputChar), .out(multiplexer_5_out),
    .sel(Instruction));  // open: in0, in1, in4, in6, in7
  Decoder #(.select(3)) decoder_2 (
    .out0(MemPointerUp), .out1(MemPointerDown), .out2(decoder_2_out2), .out3(decoder_2_out3),
    .out4(DisplayValue), .out5(ReadChar), .out6(decoder_2_out6), .out7(decoder_2_out7), .sel(Instruction),
    .en(not_1_out));
  not not_1 (not_1_out, Searching);
  not not_2 (Direction, zero_1_out_2);
  not not_3 (not_3_out, zero_2_out_2);
  not not_4 (not_4_out, clock_3_out);
  Counter #(.max('hffff), .width(16)) MemoryPointer (
    .load(MemPointerDown), .D(decrease16_1_out_2), .count(or_4_out), .Q(MemoryPointer_q), .clk(and_6_out));  // open: carry, up, clr
  DECREASE16 decrease16_1 (.in_1(MemoryPointer_q), .out_2(decrease16_1_out_2));
  RAM #(.addrWidth(16), .dataWidth(7), .enables("line")) Memory (
    .addr(MemoryPointer_q), .we(MemoryWriteEnable), .clk(and_7_out), .din(multiplexer_5_out), .dout(Value));
  and and_7 (and_7_out, MemoryWriteEnable, ExecuteCLK);
  ZERO zero_3 (.in_1(Value), .out_2(zero_3_out_2));
  and and_8 (and_8_out, Direction, clock_2_out);
  and and_9 (and_9_out, not_3_out, not_4_out);
  or or_5 (MemoryWriteEnable, decoder_2_out2, decoder_2_out3, ReadChar);
  and and_10 (SkipLoop, decoder_2_out6, zero_3_out_2);
  and and_11 (LoopBack, decoder_2_out7, ~zero_3_out_2);  // AND_Gate
  or or_6 (Searching, Direction, not_3_out);
  or or_7 (SearchCLK, and_8_out, and_9_out);

  // Notes on the sheet:
  //   I/O
  //   waiting for input
  //   CLOCK
  //   interrupts
  //   contents of Programm (hex, n*v repeats v):
  //   6 2 3 4 4 3 7 10*0 2 9*1 4*2 6 3 12*0 8*2 12*1 7 13*0 10*2 13*1 11*2 6 14*0 6*2 14*1 3 7 14*0 4 14*1
  //   8*2 6 14*0 6*2 14*1 3 7 14*0 4 14*1 4*2 6 14*0 4*3 14*1 3 7 14*0 3 4 8*2 4 5*2 4 8*3 4 14*1 5*2 6
  //   14*0 2 2 2 14*1 3 7 14*0 4 14*1 6*2 6 14*0 3 3 3 14*1 3 7 14*0 4 8*2 4 14*1 7*2 6 14*0 11*3 14*1 3 7
  //   14*0 2 2 4 14*1 7*2 6 14*0 5*2 14*1 3 7 14*0 4 14*1 6*2 6 14*0 5*2 14*1 3 7 14*0 4 11*2 4 9*3 4 14*1
  //   6*2 6 14*0 2 2 2 14*1 3 7 14*0 4 9*3 4 11*3 4 14*1 4*2 6 14*0 5*2 14*1 3 7 14*0 3 4 5*3 4 2 2 2 4
  //   14*1 9*2 6 14*0 9*3 14*1 3 7 14*0 3 4 14*1 7*2 6 14*0 3 3 3 14*1 3 7 14*0 3 4 6 3 7 6*1 2 6 7*0 5 6
  //   15*1 2 1 2 16*0 3 7 15*1 6 15*0 2 15*1 3 7 8*2 6 1 4*3 0 3 7 1 6 0 2 1 3 7 2 0 6 1 3 0 6 3 7 7 1 6 6
  //   3 7 0 3 1 7 0 2 6 3 15*0 6 15*1 2 1 2 16*0 3 7 15*1 6 15*0 2 15*1 3 7 11*2 6 1 9*3 0 3 7 1 6 0 2 1 3
  //   7 2 0 6 1 3 0 6 3 7 7 1 6 6 3 7 15*0 10*2 4 6 3 7 10*2 4 6 3 7 1 4 4 5*1 3 0 3 9*1 3 1 7 0 2 6 3
  //   15*0 6 15*1 2 1 2 16*0 3 7 15*1 6 15*0 2 15*1 3 7 10*2 6 1 6*3 0 3 7 3 1 6 0 2 1 3 7 2 0 6 1 3 0 6 3
  //   7 7 1 6 6 3 7 9*0 3 8*1 3 1 7 0 2 6 3 15*0 6 15*1 2 1 2 16*0 3 7 15*1 6 15*0 2 15*1 3 7 7*2 6 1 6*3
  //   0 3 7 3 1 6 0 2 1 3 7 2 0 6 1 3 0 6 3 7 7 1 6 6 3 7 16*0 6 12*1 2 12*0 3 7 4*1 2 11*1 3 1 7 0 2 6 3
  //   15*0 6 15*1 2 1 2 16*0 3 7 15*1 6 15*0 2 15*1 3 7 9*2 6 1 5*3 0 3 7 1 6 0 2 1 3 7 2 0 6 1 3 0 6 3 7
  //   7 1 6 6 3 7 16*0 6 12*1 2 12*0 3 7 4*1 2 11*1 3 1 7 0 2 6 3 15*0 6 15*1 2 1 2 16*0 3 7 15*1 6 15*0 2
  //   15*1 3 7 7*2 6 1 6*3 0 3 7 1 6 0 2 1 3 7 2 0 6 1 3 0 6 3 7 7 1 6 6 3 7 16*0 6 12*1 2 12*0 3 7 4*1 2
  //   11*1 3 1 7 0 2 6 3 15*0 6 15*1 2 1 2 16*0 3 7 15*1 6 15*0 2 15*1 3 7 6*2 6 1 8*3 0 3 7 2 1 6 0 2 1 3
  //   7 2 0 6 1 3 0 6 3 7 7 1 6 6 3 7 16*0 6 12*1 2 12*0 3 7 4*1 2 11*1 3 1 7 0 2 6 3 15*0 6 15*1 2 1 2
  //   16*0 3 7 15*1 6 15*0 2 15*1 3 7 6*2 6 1 6*3 0 3 7 3 1 6 0 2 1 3 7 2 0 6 1 3 0 6 3 7 7 1 6 6 3 7 16*0
  //   6 12*1 2 12*0 3 7 4*1 2 11*1 3 1 7 0 2 6 3 15*0 6 15*1 2 1 2 16*0 3 7 15*1 6 15*0 2 15*1 3 7 8*2 6 1
  //   12*3 0 3 7 2 2 1 6 0 2 1 3 7 2 0 6 1 3 0 6 3 7 7 1 6 6 3 7 16*0 6 12*1 2 12*0 3 7 4*1 2 11*1 3 1 7 0
  //   2 6 3 8*2 6 3 15*0 6*3 15*1 7 11*0 6 11*1 2 1 2 12*0 3 7 11*1 6 11*0 2 11*1 3 7 2 6 1 3 0 3 7 2 1 6
  //   0 2 1 3 7 2 0 6 1 3 0 6 3 7 7 1 6 6 3 7 0 0 6 1 2 0 3 7 1 6 0 10*2 1 3 7 15*0 6 14*1 2 14*0 3 7 15*1
  //   3 1 7 0 2 6 3 11*0 6 11*1 2 1 2 12*0 3 7 11*1 6 11*0 2 11*1 3 7 2 6 1 3 0 3 7 1 6 0 2 1 3 7 2 0 6 1
  //   3 0 6 3 7 7 1 6 6 3 7 0 0 0 6 1 1 2 0 0 3 7 1 1 6 0 0 10*2 1 1 3 7 15*0 6 13*1 2 13*0 3 7 15*1 3 1 7
  //   0 2 6 3 14*0 10*2 4 6 3 7 5*1 2 9*1 11*7 8*0 7 5*1 6 1 1 1 2 1 2 4*0 3 7 1 1 1 6 0 0 0 2 1 1 1 3 7
  //   7*2 6 1 6*3 0 3 7 3 1 6 0 2 1 3 7 2 0 6 1 3 0 6 3 7 7 1 6 6 3 7 0 0 6 9*0 2 9*1 3 7 0 6 8*0 2 8*1 3
  //   7 1 1 1 7 4*0 6 1 1 1 2 1 2 4*0 3 7 1 1 1 6 0 0 0 2 1 1 1 3 7 7*2 6 1 6*3 0 3 7 1 6 0 2 1 3 7 2 0 6
  //   1 3 0 6 3 7 7 1 6 6 3 7 0 0 6 3 0 6 1 1 2 10*0 2 8*1 3 7 1 1 6 0 0 2 1 1 3 7 0 7 1 1 7 4*0 6 1 1 1 2
  //   1 2 4*0 3 7 1 1 1 6 0 0 0 2 1 1 1 3 7 9*2 6 1 5*3 0 3 7 1 6 0 2 1 3 7 2 0 6 1 3 0 6 3 7 7 1 6 6 3 7
  //   0 0 6 9*0 2 9*1 3 7 0 6 3 8*0 3 8*1 7 1 1 1 7 4*0 6 1 1 1 2 1 2 4*0 3 7 1 1 1 6 0 0 0 2 1 1 1 3 7
  //   6*2 6 1 8*3 0 3 7 2 1 6 0 2 1 3 7 2 0 6 1 3 0 6 3 7 7 1 6 6 3 7 0 0 0 6 1 1 2 8*0 2 6*1 3 7 1 1 6 0
  //   0 2 1 1 3 7 0 6 3 7*0 3 6 8*1 2 1 2 9*0 3 7 8*1 6 8*0 2 8*1 3 7 1 6 6 3 7 0 3 1 7 0 2 6 3 1 2 0 7 1
  //   6 6 3 7 0 0 0 6 1 1 2 8*0 2 6*1 3 7 1 1 6 0 0 2 1 1 3 7 10*0 2 11*1 7 0 0 7 1 1 7 4*0 6 1 1 1 2 1 2
  //   4*0 3 7 1 1 1 6 0 0 0 2 1 1 1 3 7 6*2 6 1 6*3 0 3 7 3 1 6 0 2 1 3 7 2 0 6 1 3 0 6 3 7 7 1 6 6 3 7 0
  //   0 0 6 1 1 2 8*0 2 6*1 3 7 1 1 6 0 0 2 1 1 3 7 0 6 3 7*0 3 6 8*1 2 1 2 9*0 3 7 8*1 6 8*0 2 8*1 3 7 1
  //   6 6 3 7 0 3 1 7 0 2 6 3 1 2 0 7 1 6 6 3 7 0 0 0 6 1 1 2 8*0 2 6*1 3 7 1 1 6 0 0 2 1 1 3 7 1 7 0 0 7
  //   0 6 8*0 2 8*1 3 7 6*0 6 0 0 3 1 1 3 7 9*1 7 4*0 6 1 1 1 2 1 2 4*0 3 7 1 1 1 6 0 0 0 2 1 1 1 3 7 8*2
  //   6 1 12*3 0 3 7 2 2 1 6 0 2 1 3 7 2 0 6 1 3 0 6 3 7 7 1 6 6 3 7 11*0 2 8*1 6 8*0 6 9*1 6 1 2 1 2 0 0
  //   3 7 1 6 0 2 1 3 7 10*0 3 7 11*1 6 11*0 2 11*1 3 7 0 0 0 3 7 1 1 1 7 10*0 6 9*1 2 1 2 10*0 3 7 9*1 6
  //   9*0 2 9*1 3 7 1 6 6 3 7 13*0 4 7*1 10*2 5*0 6 10*1 2 16*0 2 6*1 3 7 10*1 6 10*0 2 10*1 3 7 16*0 6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
  //   Programm & CU
  //   Loop Control
  //   Memory
endmodule

module INCREASE16 (
  input  [15:0] in_1,
  output [15:0] out_2
);

  Adder #(.width(16)) adder_1 (.a(in_1), .b(16'h1), .out(out_2));  // open: cin, cout
endmodule

module DECREASE16 (
  input  [15:0] in_1,
  output [15:0] out_2
);

  Subtractor #(.width(16)) subtractor_1 (.a(in_1), .b(16'h1), .out(out_2));  // open: bin, bout
endmodule

module DECREASE7 (
  input  [6:0] in_1,
  output [6:0] out_2
);

  Subtractor #(.width(7)) subtractor_1 (.a(in_1), .b(7'b0000001), .out(out_2));  // open: bin, bout
endmodule

module INCREASE7 (
  input  [6:0] in_1,
  output [6:0] out_2
);

  Adder #(.width(7)) adder_1 (.a(in_1), .b(7'b0000001), .out(out_2));  // open: cin, cout
endmodule

module ZERO (
  input  [6:0] in_1,
  output out_2
);

  Comparator #(.width(7)) comparator_1 (.a(in_1), .b({7{1'b0}}), .eq(out_2));  // open: gt, lt
endmodule
