// Logisim project cpu.circ as structural Verilog: 6 circuits, main circuit main
module main (
  input  in_1
);

  wire CLK, clock_1_out, cu_1_alu_en, cu_1_flag_wr_en, cu_1_icni, cu_1_ld12c_alu, cu_1_ldc_en, cu_1_mv_en,
       cu_1_mv_r2pc, cu_1_pc2alua, cu_1_ra_en, cu_1_reg_we, decoder_1_out1, not_1_out;
  wire [1:0] cu_1_stage;
  wire [2:0] cu_1_a, cu_1_b, cu_1_c, cu_1_r;
  wire [3:0] alu_1_flagsout, register_1_q;
  wire [4:0] cu_1_alu_cmd;
  wire [15:0] alu_1_r, bit_extender_1_out, controlled_buffer_1_out, controlled_buffer_2_out,
       controlled_buffer_4_out, cpu_register_1_porta, cpu_register_1_portb, cpu_register_1_portc, cu_1_ldc,
       ProgrammCounter_q;
  wire [19:0] PMemBus;

  Decoder #(.enable("false"), .select(2)) decoder_1 (
    .out1(decoder_1_out1), .sel(cu_1_stage));  // open: out0, out2, out3
  CU cu_1 (
    .CLK(CLK), .PMemBus(PMemBus), .Reset(in_1), .Flags(register_1_q), .Stage(cu_1_stage),
    .ALU_CMD(cu_1_alu_cmd), .A(cu_1_a), .B(cu_1_b), .C(cu_1_c), .R(cu_1_r), .Reg_WE(cu_1_reg_we),
    .LDC_EN(cu_1_ldc_en), .ALU_EN(cu_1_alu_en), .MV_EN(cu_1_mv_en), .MV_R2PC(cu_1_mv_r2pc),
    .LD12C_ALU(cu_1_ld12c_alu), .RA_EN(cu_1_ra_en), .PC2ALUa(cu_1_pc2alua), .Flag_WR_EN(cu_1_flag_wr_en),
    .ICNI(cu_1_icni), .LDC(cu_1_ldc));  // open: out_20, out_21, out_22
  LED InstructionError (.in(cu_1_icni));
  Clock clock_1 (.out(clock_1_out));
  and and_1 (CLK, ~cu_1_icni, clock_1_out);  // AND_Gate
  assign controlled_buffer_1_out = cu_1_ldc_en ? cu_1_ldc : 16'bz;  // Controlled_Buffer controlled_buffer_1
  assign bit_extender_1_out = {{4{cu_1_ldc[15]}}, cu_1_ldc[15:4]};  // Bit_Extender bit_extender_1
  assign controlled_buffer_2_out = cu_1_ld12c_alu ? bit_extender_1_out : 16'bz;  // Controlled_Buffer controlled_buffer_2
  CPU_Register cpu_register_1 (
    .CLK(CLK), .Reset(in_1), .AddrINP(cu_1_r), .WE(cu_1_reg_we), .PortINP(controlled_buffer_1_out),
    .AddrA(cu_1_a), .AddrB(cu_1_b), .AddrC(cu_1_c), .PortA(cpu_register_1_porta),
    .PortB(cpu_register_1_portb), .PortC(cpu_register_1_portc));
  ALU alu_1 (
    .Flags(register_1_q), .a(controlled_buffer_4_out), .b(controlled_buffer_2_out), .c(cpu_register_1_portc),
    .CMD(cu_1_alu_cmd), .flagsOut(alu_1_flagsout), .R(alu_1_r));
  assign controlled_buffer_1_out = cu_1_mv_en ? cpu_register_1_porta : 16'bz;  // Controlled_Buffer controlled_buffer_3
  assign controlled_buffer_4_out = cu_1_ra_en ? cpu_register_1_porta : 16'bz;  // Controlled_Buffer controlled_buffer_4
  assign controlled_buffer_2_out = not_1_out ? cpu_register_1_portb : 16'bz;  // Controlled_Buffer controlled_buffer_5
  assign controlled_buffer_1_out = cu_1_alu_en ? alu_1_r : 16'bz;  // Controlled_Buffer controlled_buffer_6
  Register #(.width(4)) register_1 (
    .D(alu_1_flagsout), .en(cu_1_flag_wr_en), .Q(register_1_q), .clk(CLK));  // open: clr
  not not_1 (not_1_out, cu_1_ld12c_alu);
  assign controlled_buffer_4_out = cu_1_pc2alua ? ProgrammCounter_q : 16'bz;  // Controlled_Buffer controlled_buffer_7
  Counter #(.max('hffff), .width(16)) ProgrammCounter (
    .clr(in_1), .load(cu_1_mv_r2pc), .count(decoder_1_out1), .clk(CLK), .D(controlled_buffer_1_out),
    .Q(ProgrammCounter_q));  // open: up, carry
  ROM #(.addrWidth(16), .dataWidth(20)) PRG_MEM (.addr(ProgrammCounter_q), .data(PMemBus));

  // Other names for the same wires on the sheet: Reset = in_1

  // Notes on the sheet:
  //   contents of PRG_MEM (hex, n*v repeats v):
  //   160 f 560 f 4*0 ff960
endmodule

module ALU (
  input  [3:0] Flags,
  input  [15:0] a,
  input  [15:0] b,
  input  [15:0] c,
  input  [4:0] CMD,
  output [3:0] flagsOut,
  output [15:0] R
);

  wire adder_1_cout, adder_2_cout, adder_3_cout, adder_4_cout, subtractor_1_bout;
  wire [15:0] adder_1_out, adder_2_out, adder_3_out, adder_4_out, subtractor_1_out;

  Adder #(.width(16)) adder_1 (.a(a), .b(b), .out(adder_1_out), .cin(Flags[0]), .cout(adder_1_cout));
  Adder #(.width(16)) adder_2 (.a(a), .b(b), .out(adder_2_out), .cout(adder_2_cout));  // open: cin
  Adder #(.width(16)) adder_3 (.a(adder_1_out), .b(c), .out(adder_3_out), .cin(adder_1_cout), .cout(adder_3_cout));
  Adder #(.width(16)) adder_4 (.a(a), .b(b), .out(adder_4_out), .cin(Flags[0]), .cout(adder_4_cout));
  Subtractor #(.width(16)) subtractor_1 (
    .a(a), .b(b), .out(subtractor_1_out), .bin(Flags[0]), .bout(subtractor_1_bout));
  nor16 nor16_1 (.in_1(R), .out_2(flagsOut[2]));
  Multiplexer #(.select(5)) multiplexer_1 (
    .in0(adder_2_cout), .in1(adder_3_cout), .in2(adder_4_cout), .in3(subtractor_1_bout), .out(flagsOut[0]),
    .sel(CMD));  // open: in4, in5, in6, in7, in8, in9, in10, in11, in12, in13, in14, in15, in16, in17, in18, in19, in20, in21, in22, in23, in24, in25, in26, in27, in28, in29, in30, in31
  Multiplexer #(.select(5), .width(16)) multiplexer_2 (
    .in0(adder_2_out), .in1(adder_3_out), .in2(adder_4_out), .in3(subtractor_1_out), .out(R), .sel(CMD));  // open: in4, in5, in6, in7, in8, in9, in10, in11, in12, in13, in14, in15, in16, in17, in18, in19, in20, in21, in22, in23, in24, in25, in26, in27, in28, in29, in30, in31

  // Notes on the sheet:
  //   ADD a b c
  //   ADD a b
  //   ADD a b carry
  //   SUB a b
  //   Zero Flag 2
  //   Carry Flag 0
endmodule

module CU (
  input  CLK,
  input  [19:0] PMemBus,
  input  Reset,
  input  [3:0] Flags,
  output [1:0] Stage,
  output [4:0] ALU_CMD,
  output [2:0] A,
  output [2:0] B,
  output [2:0] C,
  output [2:0] R,
  output Reg_WE,
  output LDC_EN,
  output ALU_EN,
  output MV_EN,
  output MV_R2PC,
  output LD12C_ALU,
  output RA_EN,
  output PC2ALUa,
  output Flag_WR_EN,
  output out_20,
  output out_21,
  output out_22,
  output ICNI,
  output [15:0] LDC
);

  wire and_1_out, bitselector_1_out, Fetch, ldc_select_1_ldc_active;
  wire [3:0] MikroOp_data;
  wire [7:0] ldc_select_1_opcode_const, multiplexer_2_out;
  wire [7:5] InstructionWord_q;
  wire [9:2] register_1_q;

  Register #(.width(20)) InstructionWord (
    .D(PMemBus), .en(Fetch), .clk(CLK), .Q({LDC[15:13], C, B, A, InstructionWord_q, ALU_CMD}), .clr(Reset));
  Counter #(.max('h3), .width(2)) StageCounter (.clk(CLK), .Q(Stage));  // open: clr, load, up, count, D, carry
  Multiplexer #(.width(3)) multiplexer_1 (
    .in0(LDC[15:13]), .in1({InstructionWord_q[6:5], ALU_CMD[4]}), .out(R), .sel(ldc_select_1_ldc_active));
  Decoder #(.enable("false"), .select(2)) decoder_1 (.out0(Fetch), .sel(Stage));  // open: out1, out2, out3
  BitSelector #(.width(4)) bitselector_1 (.in(Flags), .out(bitselector_1_out), .sel(MikroOp_data[2:1]));
  and and_1 (and_1_out, ~bitselector_1_out, MikroOp_data[3]);  // AND_Gate
  LDC_select ldc_select_1 (
    .OpCode({InstructionWord_q, ALU_CMD}), .OpCode_const(ldc_select_1_opcode_const),
    .LDC_active(ldc_select_1_ldc_active));
  Multiplexer #(.width(8)) multiplexer_2 (
    .in0(8'h6c), .in1(ldc_select_1_opcode_const), .out(multiplexer_2_out), .sel(and_1_out));
  ROM #(.addrWidth(10), .dataWidth(16)) MikroOp (
    .addr({register_1_q, Stage}),
    .data({out_22, out_21, out_20, Flag_WR_EN, PC2ALUa, RA_EN, LD12C_ALU, MV_R2PC, MV_EN, ALU_EN, LDC_EN, Reg_WE, MikroOp_data}));
  Register register_1 (.D(multiplexer_2_out), .Q(register_1_q), .clk(CLK));  // open: en, clr
  not not_1 (ICNI, MikroOp_data[0]);

  assign LDC[12:0] = {C, B, A, ALU_CMD[3:0]};

  // Notes on the sheet:
  //   xxxxRRR1xxxxxxxxxxxx
  //   Load Constant
  //   6C = NOP
  //   contents of MikroOp (hex, n*v repeats v):
  //   1 1 41 51 8*0 1 1 41 51 240*0 1 1 81 181 28*0 1 81 81 91 92*0 1 a01 a41 b41 124*0 1 1 31 31
  //   EN Enable
  //   WE Write Enable
  //   +0010
  //   +0020
  //   +0040
  //   +0080
  //   +0100
  //   +0200
  //   +0400
  //   +0800
  //   +1000
  //   Move Enable
  //   Move Register to Programm Counter
  //   Enable Register A ALU
  //   Instruction Code Not Implemented
  //   LOAD 12 Bit signed Constant into ALU
  //   Programm Counter To Alu Port a
endmodule

module nor16 (
  input  [15:0] in_1,
  output out_2
);

  nor nor_1 (out_2, in_1[0], in_1[1], in_1[2], in_1[3], in_1[4], in_1[5], in_1[6], in_1[7], in_1[8], in_1[9], in_1[10], in_1[11], in_1[12], in_1[13], in_1[14], in_1[15]);
endmodule

module CPU_Register (
  input  CLK,
  input  Reset,
  input  [2:0] AddrINP,
  input  WE,
  input  [15:0] PortINP,
  input  [2:0] AddrA,
  input  [2:0] AddrB,
  input  [2:0] AddrC,
  output [15:0] PortA,
  output [15:0] PortB,
  output [15:0] PortC
);

  wire decoder_1_out0, decoder_1_out1, decoder_1_out2, decoder_1_out3, decoder_1_out4, decoder_1_out5,
       decoder_1_out6, decoder_1_out7;
  wire [15:0] register_1_q, register_2_q, register_3_q, register_4_q, register_5_q, register_6_q,
       register_7_q, register_8_q;

  Decoder #(.select(3)) decoder_1 (
    .out0(decoder_1_out0), .out1(decoder_1_out1), .out2(decoder_1_out2), .out3(decoder_1_out3),
    .out4(decoder_1_out4), .out5(decoder_1_out5), .out6(decoder_1_out6), .out7(decoder_1_out7),
    .sel(AddrINP), .en(WE));
  Register #(.width(16)) register_1 (.D(PortINP), .en(decoder_1_out0), .clk(CLK), .Q(register_1_q), .clr(Reset));
  Register #(.width(16)) register_2 (.D(PortINP), .en(decoder_1_out1), .clk(CLK), .Q(register_2_q), .clr(Reset));
  Register #(.width(16)) register_3 (.D(PortINP), .en(decoder_1_out2), .clk(CLK), .Q(register_3_q), .clr(Reset));
  Register #(.width(16)) register_4 (.D(PortINP), .en(decoder_1_out3), .clk(CLK), .Q(register_4_q), .clr(Reset));
  Register #(.width(16)) register_5 (.D(PortINP), .en(decoder_1_out4), .clk(CLK), .Q(register_5_q), .clr(Reset));
  Register #(.width(16)) register_6 (.D(PortINP), .en(decoder_1_out5), .clk(CLK), .Q(register_6_q), .clr(Reset));
  Register #(.width(16)) register_7 (.D(PortINP), .en(decoder_1_out6), .clk(CLK), .Q(register_7_q), .clr(Reset));
  Register #(.width(16)) register_8 (.D(PortINP), .en(decoder_1_out7), .clk(CLK), .Q(register_8_q), .clr(Reset));
  Multiplexer #(.select(3), .width(16)) multiplexer_1 (
    .in0(register_1_q), .in1(register_2_q), .in2(register_3_q), .in3(register_4_q), .in4(register_5_q),
    .in5(register_6_q), .in6(register_7_q), .in7(register_8_q), .out(PortC), .sel(AddrC));
  Multiplexer #(.select(3), .width(16)) multiplexer_2 (
    .in0(register_1_q), .in1(register_2_q), .in2(register_3_q), .in3(register_4_q), .in4(register_5_q),
    .in5(register_6_q), .in6(register_7_q), .in7(register_8_q), .out(PortA), .sel(AddrA));
  Multiplexer #(.select(3), .width(16)) multiplexer_3 (
    .in0(register_1_q), .in1(register_2_q), .in2(register_3_q), .in3(register_4_q), .in4(register_5_q),
    .in5(register_6_q), .in6(register_7_q), .in7(register_8_q), .out(PortB), .sel(AddrB));

  // Notes on the sheet:
  //   DONT TOUCH
endmodule

module LDC_select (
  input  [7:0] OpCode,
  output [7:0] OpCode_const,
  output LDC_active
);

  wire not_1_out;

  not not_1 (not_1_out, OpCode[7]);
  Multiplexer #(.width(8)) multiplexer_1 (.in0(8'h80), .in1(OpCode), .out(OpCode_const), .sel(not_1_out));

  assign LDC_active = OpCode[7];
endmodule
